# Fritzing sketch Knock Detector (saved by Fritzing 0.7.10b)
breadboards: 1

parts:
  Arduino_Uno = Arduino
  Piezo_Vibration_Sensor = Piezo Speaker
  1MΩ = Resistor [tolerance=±5% resistance=1M package=THT]
  220Ω = Resistor [tolerance=±5% resistance=220 package=THT]
  part = Resistor [tolerance=±5% resistance=220 package=THT]
  part_2 = Resistor [tolerance=±5% resistance=220 package=THT]
  RGB_LED = RGB LED - (4 legs) [package="5 mm [THT]"]
  Relay = Relay [package=THT]
  12v_Battery = 4 x AAA Battery Mount
  1kΩ = 1k Ω Resistor [package=THT]
  Door_Strike = DC Motor
  Diode = Rectifier Diode [package=THT]

nets:
  N1: Arduino_Uno.GND, Piezo_Vibration_Sensor.pin1, 1MΩ.Pin_1, Relay.COIL1, Diode.cathode
  N2: Arduino_Uno.D8, Relay.COIL2, Diode.anode
  N3: Arduino_Uno.D6, 220Ω.Pin_1
  N4: Arduino_Uno.D5, part.Pin_1
  N5: Arduino_Uno.D3, part_2.Pin_0
  N6: Arduino_Uno.+5V, RGB_LED.common_anode
  N7: Arduino_Uno.A0, Piezo_Vibration_Sensor.pin2, 1MΩ.Pin_0
  N8: 220Ω.Pin_0, RGB_LED.red_cathode
  N9: part.Pin_0, RGB_LED.green_cathode
  N10: part_2.Pin_1, RGB_LED.blue_cathode
  N11: Relay.A, 1kΩ.Pin_1
  N12: Relay.C1, Relay.C2, 12v_Battery.+
  N13: Relay.B, Door_Strike.pin_2
  N14: 12v_Battery.-, 1kΩ.Pin_0, Door_Strike.pin_1
